# Fritzing sketch lesson1-diagram (saved by Fritzing 0.9.3b)
breadboards: 1

parts:
  Part1 = Photon
  S1 = Pushbutton [package="[SMD]"]

nets:
  N1: Part1.GND, S1.Pin_1, S1.Pin_2
  N2: Part1.D0, S1.Pin_3, S1.Pin_4
