# Fritzing sketch lesson2-diagram (saved by Fritzing 0.9.3b)
breadboards: 1

parts:
  LED1 = smd LED [color="Red (633nm)" package="1206 [SMD]"]
  LED2 = smd LED [color="Green (555nm)" package="1206 [SMD]"]
  Part1 = Photon
  J1 = Piezo Speaker
  S1 = Pushbutton [package="[THT]"]
  U1 = POT [package=pot_alpha_rv16af-20]
  R1 = Photocell (LDR) [package=THT]
  R2 = Resistor [tolerance=±5% resistance=10k package="2010 [SMD]"]

nets:
  N1: LED1.cathode, LED2.cathode, Part1.GND, J1.pin1, S1.Pin_1, S1.Pin_2, U1.E, R2.Pin_0
  N2: LED1.anode, Part1.D0
  N3: LED2.anode, Part1.DAC
  N4: Part1.A0, U1.S
  N5: Part1.A2, R1.pin_0, R2.Pin_1
  N6: Part1.A4, R1.pin_1
  N7: Part1.D2, J1.pin2
  N8: Part1.D4, S1.Pin_3, S1.Pin_4
  N9: Part1.3V3, U1.A
