# Fritzing sketch lesson3-diagram (saved by Fritzing 0.9.3b)
breadboards: 1

parts:
  Part1 = Photon
  U1 = POT [package=pot_mammoth]
  J1 = Basic Servo
  PIR1 = PIR sensor

nets:
  N1: Part1.A0, U1.A
  N2: Part1.A2, PIR1.SIG
  N3: Part1.A4, J1.pulse
  GND: Part1.GND, U1.S, J1.gnd, PIR1.GND
  VIN: Part1.VIN, J1.vcc, PIR1.VDD
  N4: Part1.3V3, U1.E
